# Fritzing sketch Untitled Sketch (saved by Fritzing 0.9.10b)

parts:
  M1 = DOIT Esp32 DevKit v1 (30 pins long, 11 pins width) [part_number=ESP32S-PIN30]
  W5500_Module1 = W5500 Ethernet module [package="DIP (Dual Inline) [THT]"]
  ZS-042_RTC1 = ZS-042 RTC Module

nets:
  3V3: M1.3V3, ZS-042_RTC1.VCC
  GND: M1.GND, W5500_Module1.GND, ZS-042_RTC1.GND
  N1: M1.D15, W5500_Module1.INT
  N2: M1.D4, W5500_Module1.RST
  N3: M1.D5, W5500_Module1.SCS
  N4: M1.D18, W5500_Module1.SCLK
  N5: M1.D19, W5500_Module1.MISO
  N6: M1.D21, ZS-042_RTC1.SDA
  N7: M1.D22, ZS-042_RTC1.SCL
  N8: M1.D23, W5500_Module1.MOSI
  VIN: M1.VIN, W5500_Module1.5V

custom parts:
  DOIT Esp32 DevKit v1 (30 pins long, 11 pins width): The DOIT Esp32 DevKit v1 is one of the development board created by DOIT to evaluate the ESP-WROOM-32 module. It is based on the ESP32 microcontroller that boasts Wifi, Bluetooth, Ethernet and Low Power support all in a single chip. (vanepp) made breadboard work, adjusted pin numbering and labels and reduced size of schematic and cleaned up pcb. This chip is 30pins long (2 x15) and 11 pins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
  W5500 Ethernet module: W5500 based SPI Ethernet module for Arduino, etc.
